# Fritzing sketch pi4b+uln2003+28byj-48 (saved by Fritzing 0.9.4)

parts:
  Raspberry_Pi_1 = Raspberry Pi 4 [part_number=RPI-4-b]
  MOTOR1 = 28BYJ-48 Stepper Motor
  BREAKOUT1 = ULN2003A breakout board

nets:
  N1: Raspberry_Pi_1.GPIO4, BREAKOUT1.In_1
  N2: Raspberry_Pi_1.GPIO17, BREAKOUT1.In_2
  N3: Raspberry_Pi_1.GPIO24, BREAKOUT1.In_4
  N4: Raspberry_Pi_1.GPIO23, BREAKOUT1.In_3
  N5: Raspberry_Pi_1.GND, BREAKOUT1.0V
  5V: Raspberry_Pi_1.5V, BREAKOUT1.+5V
  N6: MOTOR1.RED, BREAKOUT1.RED_wire
  N7: MOTOR1.ORANGE, BREAKOUT1.ORANGE_wire
  N8: MOTOR1.YELLOW, BREAKOUT1.YELLOW_wire
  N9: MOTOR1.PINK, BREAKOUT1.PINK_wire
  N10: MOTOR1.BLUE, BREAKOUT1.BLUE_wire

custom parts:
  Raspberry Pi 4: The RPi4, a faster version of the awesome Raspberry Pi 2 B ARM Board with 40 pin gpio. Ready for special Raspberry Pi B+ and RPi2 Hat (Hardware attached (on) top)
  ULN2003A breakout board: ULN2003A 7-way Darlington Transistor Driver on breakoutboard
