# Fritzing sketch piPico+uln2003+28byj-48 (saved by Fritzing 0.9.4)

parts:
  Mod1 = Raspberry Pi Pico
  BREAKOUT1 = ULN2003A breakout board
  MOTOR1 = 28BYJ-48 Stepper Motor

nets:
  N1: Mod1.pin_29, BREAKOUT1.In_1
  N2: Mod1.pin_31, BREAKOUT1.In_2
  N3: Mod1.pin_32, BREAKOUT1.In_3
  N4: Mod1.pin_34, BREAKOUT1.In_4
  N5: Mod1.pin_38, BREAKOUT1.0V
  N6: Mod1.pin_40, BREAKOUT1.+5V
  N7: BREAKOUT1.RED_wire, MOTOR1.RED
  N8: BREAKOUT1.ORANGE_wire, MOTOR1.ORANGE
  N9: BREAKOUT1.YELLOW_wire, MOTOR1.YELLOW
  N10: BREAKOUT1.PINK_wire, MOTOR1.PINK
  N11: BREAKOUT1.BLUE_wire, MOTOR1.BLUE

custom parts:
  Raspberry Pi Pico: Raspberry Pi Pico. Based around the RP2040 microcontroller the Pico is a low cost microcontroller device bringing Raspberry Pi quality, cost, and easy of use to the microcontroller space. Jan 2021, Split part in to two versions: tht (this one) and SMD. This one will drill holes for a .1 in header in pcb to allow plugging in the module as well as providing pads to solder the module to the top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
  ULN2003A breakout board: ULN2003A 7-way Darlington Transistor Driver on breakoutboard
